# Fritzing sketch at-me (saved by Fritzing 0.9.5d)
circuit board: 8.46667cm x 5.64444cm
breadboards: 1

parts:
  Componente1 = Arduino Nano (Rev3.0)
  DFRobot_DFPlayer_Mini1 = DFRobot DFPlayer Mini [part_number=DFR0299]
  SP1 = SPEAKER [package=pcb_mount_speaker]
  S1 = SWITCH-MOMENTARY-2 [package=tactile-pth-12mm]

nets:
  N1: Componente1.GND, DFRobot_DFPlayer_Mini1.GND-1, DFRobot_DFPlayer_Mini1.GND-2, S1.2
  N2: Componente1.D6, S1.1
  N3: Componente1.D10, DFRobot_DFPlayer_Mini1.TX
  N4: Componente1.D11/MOSI, DFRobot_DFPlayer_Mini1.RX
  5V: Componente1.5V, DFRobot_DFPlayer_Mini1.VCC
  N5: DFRobot_DFPlayer_Mini1.SPK_1, SP1.+
  N6: DFRobot_DFPlayer_Mini1.SPK_2, SP1.-
